# Fritzing sketch 9 (saved by Fritzing 0.9.4)
breadboards: 1

parts:
  U1 = NodeMCU V1.0
  R1 = Resistor [tolerance=±5% resistance=220 package=THT]
  LED1 = LED - 5mm [color="Red (633nm)" package="5 mm [THT]"]
  part = HC-SR501 Body Sensor Module

nets:
  N1: U1.D1, part.OUT
  N2: U1.3V3#5, part.VCC
  N3: U1.GND#6, R1.Pin_0, part.GND
  N4: U1.D6, LED1.anode
  N5: R1.Pin_1, LED1.cathode

custom parts:
  NodeMCU V1.0: ESP8266 based NodeMCU V1.0
  HC-SR501 Body Sensor Module: Pyroelectric Infrared PIR Motion Sensor Detector Module
